// Logisim project GPU_Test.circ as structural Verilog: 1 circuit, main circuit main
module main (
);

  wire counter_1_carry, counter_2_carry, rgb_video_1_p1, rgb_video_1_p2, rgb_video_1_p4, rgb_video_1_p5;
  wire [7:0] counter_1_q, rgb_video_1_p7;

  Counter counter_1 (
    .clr(1'b0), .clk(rgb_video_1_p1), .carry(counter_1_carry), .Q(counter_1_q));  // open: load, up, count, D
  // RGB_Video #(.height(256), .width(256)) rgb_video_1: pin names not known; wires that end beside it: rgb_video_1_p1, rgb_video_1_p2, 1'b0, rgb_video_1_p4, rgb_video_1_p5, counter_1_q, rgb_video_1_p7, rgb_video_1_p2
  Clock clock_1 (.out(rgb_video_1_p4));
  Counter counter_2 (
    .clr(1'b0), .load(1'b0), .up(rgb_video_1_p5), .count(rgb_video_1_p5), .clk(counter_1_carry),
    .carry(counter_2_carry), .Q(rgb_video_1_p7));  // open: D
  not not_1 (rgb_video_1_p5, counter_2_carry);
endmodule
