// Logisim project Intial_ALU_design.circ as structural Verilog: 2 circuits, main circuit ALU
module ALU (
  input  [3:0] Operation,
  input  [31:0] Operand_A,
  input  [31:0] Ooerand_B,
  output [31:0] Result,
  output Wero
);

  wire one_bit_alu_1_out_7, one_bit_alu_2_out_7, one_bit_alu_3_out_7, one_bit_alu_4_out_7,
       one_bit_alu_5_out_7, one_bit_alu_6_out_7, one_bit_alu_7_out_7, one_bit_alu_8_out_7,
       one_bit_alu_9_out_7, one_bit_alu_10_out_7, one_bit_alu_11_out_7, one_bit_alu_12_out_7,
       one_bit_alu_13_out_7, one_bit_alu_14_out_7, one_bit_alu_15_out_7, one_bit_alu_16_out_7,
       one_bit_alu_17_out_7, one_bit_alu_18_out_7, one_bit_alu_19_out_7, one_bit_alu_20_out_7,
       one_bit_alu_21_out_7, one_bit_alu_22_out_7, one_bit_alu_23_out_7, one_bit_alu_24_out_7,
       one_bit_alu_25_out_7, one_bit_alu_26_out_7, one_bit_alu_27_out_7, one_bit_alu_28_out_7,
       one_bit_alu_29_out_7, one_bit_alu_30_out_7, one_bit_alu_31_out_7, or_1_out, or_2_out;

  or or_1 (or_1_out, Operation[2], Operation[3]);
  one_bit_ALU one_bit_alu_1 (
    .A(Operand_A[0]), .B(Ooerand_B[0]), .out_6(Result[0]), .CarryIn(or_1_out), .out_7(one_bit_alu_1_out_7),
    .Control_line(Operation));  // open: Less
  one_bit_ALU one_bit_alu_2 (
    .A(Operand_A[1]), .B(Ooerand_B[1]), .Less(1'b0), .out_6(Result[1]), .CarryIn(one_bit_alu_1_out_7),
    .out_7(one_bit_alu_2_out_7), .Control_line(Operation));
  one_bit_ALU one_bit_alu_3 (
    .A(Operand_A[2]), .B(Ooerand_B[2]), .Less(1'b0), .out_6(Result[2]), .CarryIn(one_bit_alu_2_out_7),
    .out_7(one_bit_alu_3_out_7), .Control_line(Operation));
  one_bit_ALU one_bit_alu_4 (
    .A(Operand_A[3]), .B(Ooerand_B[3]), .Less(1'b0), .out_6(Result[3]), .CarryIn(one_bit_alu_3_out_7),
    .out_7(one_bit_alu_4_out_7), .Control_line(Operation));
  one_bit_ALU one_bit_alu_5 (
    .A(Operand_A[4]), .B(Ooerand_B[4]), .Less(1'b0), .out_6(Result[4]), .CarryIn(one_bit_alu_4_out_7),
    .out_7(one_bit_alu_5_out_7), .Control_line(Operation));
  one_bit_ALU one_bit_alu_6 (
    .A(Operand_A[5]), .B(Ooerand_B[5]), .Less(1'b0), .out_6(Result[5]), .CarryIn(one_bit_alu_5_out_7),
    .out_7(one_bit_alu_6_out_7), .Control_line(Operation));
  one_bit_ALU one_bit_alu_7 (
    .A(Operand_A[6]), .B(Ooerand_B[6]), .Less(1'b0), .out_6(Result[6]), .CarryIn(one_bit_alu_6_out_7),
    .out_7(one_bit_alu_7_out_7), .Control_line(Operation));
  one_bit_ALU one_bit_alu_8 (
    .A(Operand_A[7]), .B(Ooerand_B[7]), .Less(1'b0), .out_6(Result[7]), .CarryIn(one_bit_alu_7_out_7),
    .out_7(one_bit_alu_8_out_7), .Control_line(Operation));
  one_bit_ALU one_bit_alu_9 (
    .A(Operand_A[8]), .B(Ooerand_B[8]), .Less(1'b0), .out_6(Result[8]), .CarryIn(one_bit_alu_8_out_7),
    .out_7(one_bit_alu_9_out_7), .Control_line(Operation));
  one_bit_ALU one_bit_alu_10 (
    .A(Operand_A[9]), .B(Ooerand_B[9]), .Less(1'b0), .out_6(Result[9]), .CarryIn(one_bit_alu_9_out_7),
    .out_7(one_bit_alu_10_out_7), .Control_line(Operation));
  one_bit_ALU one_bit_alu_11 (
    .A(Operand_A[10]), .B(Ooerand_B[10]), .Less(1'b0), .out_6(Result[10]), .CarryIn(one_bit_alu_10_out_7),
    .out_7(one_bit_alu_11_out_7), .Control_line(Operation));
  one_bit_ALU one_bit_alu_12 (
    .A(Operand_A[11]), .B(Ooerand_B[11]), .Less(1'b0), .out_6(Result[11]), .CarryIn(one_bit_alu_11_out_7),
    .out_7(one_bit_alu_12_out_7), .Control_line(Operation));
  one_bit_ALU one_bit_alu_13 (
    .A(Operand_A[12]), .B(Ooerand_B[12]), .Less(1'b0), .out_6(Result[12]), .CarryIn(one_bit_alu_12_out_7),
    .out_7(one_bit_alu_13_out_7), .Control_line(Operation));
  one_bit_ALU one_bit_alu_14 (
    .A(Operand_A[13]), .B(Ooerand_B[13]), .Less(1'b0), .out_6(Result[13]), .CarryIn(one_bit_alu_13_out_7),
    .out_7(one_bit_alu_14_out_7), .Control_line(Operation));
  one_bit_ALU one_bit_alu_15 (
    .A(Operand_A[14]), .B(Ooerand_B[14]), .Less(1'b0), .out_6(Result[14]), .CarryIn(one_bit_alu_14_out_7),
    .out_7(one_bit_alu_15_out_7), .Control_line(Operation));
  one_bit_ALU one_bit_alu_16 (
    .A(Operand_A[15]), .B(Ooerand_B[15]), .Less(1'b0), .out_6(Result[15]), .CarryIn(one_bit_alu_15_out_7),
    .out_7(one_bit_alu_16_out_7), .Control_line(Operation));
  one_bit_ALU one_bit_alu_17 (
    .A(Operand_A[16]), .B(Ooerand_B[16]), .Less(1'b0), .out_6(Result[16]), .CarryIn(one_bit_alu_16_out_7),
    .out_7(one_bit_alu_17_out_7), .Control_line(Operation));
  one_bit_ALU one_bit_alu_18 (
    .A(Operand_A[17]), .B(Ooerand_B[17]), .Less(1'b0), .out_6(Result[17]), .CarryIn(one_bit_alu_17_out_7),
    .out_7(one_bit_alu_18_out_7), .Control_line(Operation));
  one_bit_ALU one_bit_alu_19 (
    .A(Operand_A[18]), .B(Ooerand_B[18]), .Less(1'b0), .out_6(Result[18]), .CarryIn(one_bit_alu_18_out_7),
    .out_7(one_bit_alu_19_out_7), .Control_line(Operation));
  one_bit_ALU one_bit_alu_20 (
    .A(Operand_A[19]), .B(Ooerand_B[19]), .Less(1'b0), .out_6(Result[19]), .CarryIn(one_bit_alu_19_out_7),
    .out_7(one_bit_alu_20_out_7), .Control_line(Operation));
  one_bit_ALU one_bit_alu_21 (
    .A(Operand_A[20]), .B(Ooerand_B[20]), .Less(1'b0), .out_6(Result[20]), .CarryIn(one_bit_alu_20_out_7),
    .out_7(one_bit_alu_21_out_7), .Control_line(Operation));
  one_bit_ALU one_bit_alu_22 (
    .A(Operand_A[21]), .B(Ooerand_B[21]), .Less(1'b0), .out_6(Result[21]), .CarryIn(one_bit_alu_21_out_7),
    .out_7(one_bit_alu_22_out_7), .Control_line(Operation));
  one_bit_ALU one_bit_alu_23 (
    .A(Operand_A[22]), .B(Ooerand_B[22]), .Less(1'b0), .out_6(Result[22]), .CarryIn(one_bit_alu_22_out_7),
    .out_7(one_bit_alu_23_out_7), .Control_line(Operation));
  one_bit_ALU one_bit_alu_24 (
    .A(Operand_A[23]), .B(Ooerand_B[23]), .Less(1'b0), .out_6(Result[23]), .CarryIn(one_bit_alu_23_out_7),
    .out_7(one_bit_alu_24_out_7), .Control_line(Operation));
  one_bit_ALU one_bit_alu_25 (
    .A(Operand_A[24]), .B(Ooerand_B[24]), .Less(1'b0), .out_6(Result[24]), .CarryIn(one_bit_alu_24_out_7),
    .out_7(one_bit_alu_25_out_7), .Control_line(Operation));
  one_bit_ALU one_bit_alu_26 (
    .A(Operand_A[25]), .B(Ooerand_B[25]), .Less(1'b0), .out_6(Result[25]), .CarryIn(one_bit_alu_25_out_7),
    .out_7(one_bit_alu_26_out_7), .Control_line(Operation));
  one_bit_ALU one_bit_alu_27 (
    .A(Operand_A[26]), .B(Ooerand_B[26]), .Less(1'b0), .out_6(Result[26]), .CarryIn(one_bit_alu_26_out_7),
    .out_7(one_bit_alu_27_out_7), .Control_line(Operation));
  one_bit_ALU one_bit_alu_28 (
    .A(Operand_A[27]), .B(Ooerand_B[27]), .Less(1'b0), .out_6(Result[27]), .CarryIn(one_bit_alu_27_out_7),
    .out_7(one_bit_alu_28_out_7), .Control_line(Operation));
  one_bit_ALU one_bit_alu_29 (
    .A(Operand_A[28]), .B(Ooerand_B[28]), .Less(1'b0), .out_6(Result[28]), .CarryIn(one_bit_alu_28_out_7),
    .out_7(one_bit_alu_29_out_7), .Control_line(Operation));
  one_bit_ALU one_bit_alu_30 (
    .A(Operand_A[29]), .B(Ooerand_B[29]), .Less(1'b0), .out_6(Result[29]), .CarryIn(one_bit_alu_29_out_7),
    .out_7(one_bit_alu_30_out_7), .Control_line(Operation));
  one_bit_ALU one_bit_alu_31 (
    .A(Operand_A[30]), .B(Ooerand_B[30]), .Less(1'b0), .out_6(Result[30]), .CarryIn(one_bit_alu_30_out_7),
    .out_7(one_bit_alu_31_out_7), .Control_line(Operation));
  one_bit_ALU one_bit_alu_32 (
    .A(Operand_A[31]), .B(Ooerand_B[31]), .Less(1'b0), .out_6(Result[31]), .CarryIn(one_bit_alu_31_out_7),
    .Control_line(Operation));  // open: out_7
  or or_2 (or_2_out, Result[0], Result[1], Result[2], Result[3], Result[4], Result[5], Result[6], Result[7], Result[8], Result[9], Result[10], Result[11], Result[12], Result[13], Result[14], Result[15], Result[16], Result[17], Result[18], Result[19], Result[20], Result[21], Result[22], Result[23], Result[24], Result[25], Result[26], Result[27], Result[28], Result[29], Result[30], Result[31]);
  not not_1 (Wero, or_2_out);
endmodule

module one_bit_ALU (
  input  [3:0] Control_line,
  input  CarryIn,
  input  A,
  input  B,
  input  Less,
  output out_6,
  output out_7
);

  wire adder_1_out, and_1_out, or_1_out, xor_1_out, xor_2_out;

  xor xor_1 (xor_1_out, Control_line[3], A);
  xor xor_2 (xor_2_out, Control_line[2], B);
  and and_1 (and_1_out, xor_2_out, xor_1_out);
  or or_1 (or_1_out, xor_2_out, xor_1_out);
  Adder #(.width(1)) adder_1 (.a(xor_1_out), .b(xor_2_out), .out(adder_1_out), .cin(CarryIn), .cout(out_7));
  Multiplexer #(.select(2), .enable("false")) multiplexer_1 (
    .in0(and_1_out), .in1(or_1_out), .in2(adder_1_out), .in3(Less), .out(out_6), .sel(Control_line[1:0]));
endmodule
