// Logisim project RegisterFile.circ as structural Verilog: 2 circuits, main circuit RegisterFile
module RegisterFile (
  input  [4:0] SEL_1,
  input  Write_en,
  input  [31:0] Data_Input,
  input  [4:0] SEL_1_2,
  input  [4:0] SEL_2,
  output [31:0] Out_Reg1,
  output [31:0] Out_Reg2
);

  wire clock_1_out, decoder_1_out0, decoder_1_out1, decoder_1_out2, decoder_1_out3, decoder_2_out0,
       decoder_2_out1, decoder_2_out2, decoder_2_out3, decoder_3_out0, decoder_3_out1, decoder_3_out2,
       decoder_3_out3, demultiplexer_1_out0, demultiplexer_1_out1, demultiplexer_1_out2,
       demultiplexer_1_out3, demultiplexer_1_out4, demultiplexer_1_out5, demultiplexer_1_out6,
       demultiplexer_1_out7, demultiplexer_2_out0, demultiplexer_2_out1, demultiplexer_2_out2,
       demultiplexer_2_out3, demultiplexer_2_out4, demultiplexer_2_out5, demultiplexer_2_out6,
       demultiplexer_2_out7, demultiplexer_3_out0, demultiplexer_3_out1, demultiplexer_3_out2,
       demultiplexer_3_out3, demultiplexer_3_out4, demultiplexer_3_out5, demultiplexer_3_out6,
       demultiplexer_3_out7, demultiplexer_4_out0, demultiplexer_4_out1, demultiplexer_4_out2,
       demultiplexer_4_out3, demultiplexer_4_out4, demultiplexer_4_out5, demultiplexer_4_out6,
       demultiplexer_4_out7;
  wire [31:0] multiplexer_1_out, multiplexer_2_out, multiplexer_3_out, multiplexer_4_out, multiplexer_5_out,
       multiplexer_6_out, multiplexer_7_out, multiplexer_8_out, register_1_q, register_2_q, register_3_q,
       register_4_q, register_5_q, register_6_q, register_7_q, register_8_q, register_9_q, register_10_q,
       register_11_q, register_12_q, register_13_q, register_14_q, register_15_q, register_16_q,
       register_17_q, register_18_q, register_19_q, register_20_q, register_21_q, register_22_q,
       register_23_q, register_24_q, register_25_q, register_26_q, register_27_q, register_28_q,
       register_29_q, register_30_q, register_31_q, register_32_q;

  Clock clock_1 (.out(clock_1_out));
  Demultiplexer #(.select(3)) demultiplexer_1 (
    .out0(demultiplexer_1_out0), .out1(demultiplexer_1_out1), .out2(demultiplexer_1_out2),
    .out3(demultiplexer_1_out3), .out4(demultiplexer_1_out4), .out5(demultiplexer_1_out5),
    .out6(demultiplexer_1_out6), .out7(demultiplexer_1_out7), .in(Write_en), .sel(SEL_1_2[2:0]),
    .en(decoder_3_out0));
  Register #(.width(32)) register_1 (
    .D({32{1'b0}}), .en(demultiplexer_1_out0), .clk(clock_1_out), .Q(register_1_q));  // open: clr
  Register #(.width(32)) register_2 (
    .D(Data_Input), .en(demultiplexer_1_out1), .clk(clock_1_out), .Q(register_2_q));  // open: clr
  Register #(.width(32)) register_3 (
    .D(Data_Input), .en(demultiplexer_1_out2), .clk(clock_1_out), .Q(register_3_q));  // open: clr
  Register #(.width(32)) register_4 (
    .D(Data_Input), .en(demultiplexer_1_out3), .clk(clock_1_out), .Q(register_4_q));  // open: clr
  Register #(.width(32)) register_5 (
    .D(Data_Input), .en(demultiplexer_1_out4), .clk(clock_1_out), .Q(register_5_q));  // open: clr
  Register #(.width(32)) register_6 (
    .D(Data_Input), .en(demultiplexer_1_out5), .clk(clock_1_out), .Q(register_6_q));  // open: clr
  Register #(.width(32)) register_7 (
    .D(Data_Input), .en(demultiplexer_1_out6), .clk(clock_1_out), .Q(register_7_q));  // open: clr
  Register #(.width(32)) register_8 (
    .D(Data_Input), .en(demultiplexer_1_out7), .clk(clock_1_out), .Q(register_8_q));  // open: clr
  Multiplexer #(.select(3), .width(32)) multiplexer_1 (
    .in0(register_1_q), .in1(register_2_q), .in2(register_3_q), .in3(register_4_q), .in4(register_5_q),
    .in5(register_6_q), .in6(register_7_q), .in7(register_8_q), .out(multiplexer_1_out), .sel(SEL_1[2:0]),
    .en(decoder_1_out0));
  Demultiplexer #(.select(3)) demultiplexer_2 (
    .out0(demultiplexer_2_out0), .out1(demultiplexer_2_out1), .out2(demultiplexer_2_out2),
    .out3(demultiplexer_2_out3), .out4(demultiplexer_2_out4), .out5(demultiplexer_2_out5),
    .out6(demultiplexer_2_out6), .out7(demultiplexer_2_out7), .in(Write_en), .sel(SEL_1_2[2:0]),
    .en(decoder_3_out1));
  Multiplexer #(.select(3), .width(32)) multiplexer_2 (
    .in0(register_1_q), .in1(register_2_q), .in2(register_3_q), .in3(register_4_q), .in4(register_5_q),
    .in5(register_6_q), .in6(register_7_q), .in7(register_8_q), .out(multiplexer_2_out), .sel(SEL_2[2:0]),
    .en(decoder_2_out0));
  Register #(.width(32)) register_9 (
    .D(Data_Input), .en(demultiplexer_2_out0), .clk(clock_1_out), .Q(register_9_q));  // open: clr
  Register #(.width(32)) register_10 (
    .D(Data_Input), .en(demultiplexer_2_out1), .clk(clock_1_out), .Q(register_10_q));  // open: clr
  Register #(.width(32)) register_11 (
    .D(Data_Input), .en(demultiplexer_2_out2), .clk(clock_1_out), .Q(register_11_q));  // open: clr
  Register #(.width(32)) register_12 (
    .D(Data_Input), .en(demultiplexer_2_out3), .clk(clock_1_out), .Q(register_12_q));  // open: clr
  Register #(.width(32)) register_13 (
    .D(Data_Input), .en(demultiplexer_2_out4), .clk(clock_1_out), .Q(register_13_q));  // open: clr
  Register #(.width(32)) register_14 (
    .D(Data_Input), .en(demultiplexer_2_out5), .clk(clock_1_out), .Q(register_14_q));  // open: clr
  Register #(.width(32)) register_15 (
    .D(Data_Input), .en(demultiplexer_2_out6), .clk(clock_1_out), .Q(register_15_q));  // open: clr
  Register #(.width(32)) register_16 (
    .D(Data_Input), .en(demultiplexer_2_out7), .clk(clock_1_out), .Q(register_16_q));  // open: clr
  Decoder #(.select(2), .enable("false")) decoder_1 (
    .out0(decoder_1_out0), .out1(decoder_1_out1), .out2(decoder_1_out2), .out3(decoder_1_out3),
    .sel(SEL_1[4:3]));
  Multiplexer #(.select(3), .width(32)) multiplexer_3 (
    .in0(register_9_q), .in1(register_10_q), .in2(register_11_q), .in3(register_12_q), .in4(register_13_q),
    .in5(register_14_q), .in6(register_15_q), .in7(register_16_q), .out(multiplexer_3_out), .sel(SEL_1[2:0]),
    .en(decoder_1_out1));
  Demultiplexer #(.select(3)) demultiplexer_3 (
    .out0(demultiplexer_3_out0), .out1(demultiplexer_3_out1), .out2(demultiplexer_3_out2),
    .out3(demultiplexer_3_out3), .out4(demultiplexer_3_out4), .out5(demultiplexer_3_out5),
    .out6(demultiplexer_3_out6), .out7(demultiplexer_3_out7), .in(Write_en), .sel(SEL_1_2[2:0]),
    .en(decoder_3_out2));
  Multiplexer #(.select(3), .width(32)) multiplexer_4 (
    .in0(register_9_q), .in1(register_10_q), .in2(register_11_q), .in3(register_12_q), .in4(register_13_q),
    .in5(register_14_q), .in6(register_15_q), .in7(register_16_q), .out(multiplexer_4_out), .sel(SEL_2[2:0]),
    .en(decoder_2_out1));
  Decoder #(.select(2), .enable("false")) decoder_2 (
    .out0(decoder_2_out0), .out1(decoder_2_out1), .out2(decoder_2_out2), .out3(decoder_2_out3),
    .sel(SEL_2[4:3]));
  Decoder #(.select(2), .enable("false")) decoder_3 (
    .out0(decoder_3_out0), .out1(decoder_3_out1), .out2(decoder_3_out2), .out3(decoder_3_out3),
    .sel(SEL_1_2[4:3]));
  Register #(.width(32)) register_17 (
    .D(Data_Input), .en(demultiplexer_3_out0), .clk(clock_1_out), .Q(register_17_q));  // open: clr
  Register #(.width(32)) register_18 (
    .D(Data_Input), .en(demultiplexer_3_out1), .clk(clock_1_out), .Q(register_18_q));  // open: clr
  Register #(.width(32)) register_19 (
    .D(Data_Input), .en(demultiplexer_3_out2), .clk(clock_1_out), .Q(register_19_q));  // open: clr
  Register #(.width(32)) register_20 (
    .D(Data_Input), .en(demultiplexer_3_out3), .clk(clock_1_out), .Q(register_20_q));  // open: clr
  Register #(.width(32)) register_21 (
    .D(Data_Input), .en(demultiplexer_3_out4), .clk(clock_1_out), .Q(register_21_q));  // open: clr
  Register #(.width(32)) register_22 (
    .D(Data_Input), .en(demultiplexer_3_out5), .clk(clock_1_out), .Q(register_22_q));  // open: clr
  Register #(.width(32)) register_23 (
    .D(Data_Input), .en(demultiplexer_3_out6), .clk(clock_1_out), .Q(register_23_q));  // open: clr
  Register #(.width(32)) register_24 (
    .D(Data_Input), .en(demultiplexer_3_out7), .clk(clock_1_out), .Q(register_24_q));  // open: clr
  Multiplexer #(.select(3), .width(32)) multiplexer_5 (
    .in0(register_17_q), .in1(register_18_q), .in2(register_19_q), .in3(register_20_q), .in4(register_21_q),
    .in5(register_22_q), .in6(register_23_q), .in7(register_24_q), .out(multiplexer_5_out), .sel(SEL_1[2:0]),
    .en(decoder_1_out2));
  Demultiplexer #(.select(3)) demultiplexer_4 (
    .out0(demultiplexer_4_out0), .out1(demultiplexer_4_out1), .out2(demultiplexer_4_out2),
    .out3(demultiplexer_4_out3), .out4(demultiplexer_4_out4), .out5(demultiplexer_4_out5),
    .out6(demultiplexer_4_out6), .out7(demultiplexer_4_out7), .in(Write_en), .sel(SEL_1_2[2:0]),
    .en(decoder_3_out3));
  Multiplexer #(.select(3), .width(32)) multiplexer_6 (
    .in0(register_17_q), .in1(register_18_q), .in2(register_19_q), .in3(register_20_q), .in4(register_21_q),
    .in5(register_22_q), .in6(register_23_q), .in7(register_24_q), .out(multiplexer_6_out), .sel(SEL_2[2:0]),
    .en(decoder_2_out2));
  Register #(.width(32)) register_25 (
    .D(Data_Input), .en(demultiplexer_4_out0), .clk(clock_1_out), .Q(register_25_q));  // open: clr
  Register #(.width(32)) register_26 (
    .D(Data_Input), .en(demultiplexer_4_out1), .clk(clock_1_out), .Q(register_26_q));  // open: clr
  Register #(.width(32)) register_27 (
    .D(Data_Input), .en(demultiplexer_4_out2), .clk(clock_1_out), .Q(register_27_q));  // open: clr
  Register #(.width(32)) register_28 (
    .D(Data_Input), .en(demultiplexer_4_out3), .clk(clock_1_out), .Q(register_28_q));  // open: clr
  Register #(.width(32)) register_29 (
    .D(Data_Input), .en(demultiplexer_4_out4), .clk(clock_1_out), .Q(register_29_q));  // open: clr
  Register #(.width(32)) register_30 (
    .D(Data_Input), .en(demultiplexer_4_out5), .clk(clock_1_out), .Q(register_30_q));  // open: clr
  Register #(.width(32)) register_31 (
    .D(Data_Input), .en(demultiplexer_4_out6), .clk(clock_1_out), .Q(register_31_q));  // open: clr
  Register #(.width(32)) register_32 (
    .D(Data_Input), .en(demultiplexer_4_out7), .clk(clock_1_out), .Q(register_32_q));  // open: clr
  Multiplexer #(.select(3), .width(32)) multiplexer_7 (
    .in0(register_25_q), .in1(register_26_q), .in2(register_27_q), .in3(register_28_q), .in4(register_29_q),
    .in5(register_30_q), .in6(register_31_q), .in7(register_32_q), .out(multiplexer_7_out), .sel(SEL_1[2:0]),
    .en(decoder_1_out3));
  Multiplexer #(.select(3), .width(32)) multiplexer_8 (
    .in0(register_25_q), .in1(register_26_q), .in2(register_27_q), .in3(register_28_q), .in4(register_29_q),
    .in5(register_30_q), .in6(register_31_q), .in7(register_32_q), .out(multiplexer_8_out), .sel(SEL_2[2:0]),
    .en(decoder_2_out3));
  assign Out_Reg1 = multiplexer_1_out | multiplexer_3_out | multiplexer_5_out | multiplexer_7_out;  // OR_Gate or_1, 32 bits wide
  assign Out_Reg2 = multiplexer_8_out | multiplexer_6_out | multiplexer_4_out | multiplexer_2_out;  // OR_Gate or_2, 32 bits wide
endmodule

module main (
  input  [4:0] in_1,
  input  [4:0] in_2,
  input  [31:0] in_3,
  input  [4:0] in_4,
  output [31:0] out_5,
  output [31:0] out_6
);

  RegisterFile registerfile_1 (
    .SEL_1(in_1), .Data_Input(in_3), .SEL_1_2(in_4), .SEL_2(in_2), .Out_Reg1(out_5), .Out_Reg2(out_6));  // open: Write_en
endmodule
