// Logisim project Single_Cycle_design.circ as structural Verilog: 11 circuits, main circuit Register File
module Data_Path (
  input  clear,
  output [15:0] out_2,
  output [1:0] out_3,
  output [15:0] out_4,
  output [15:0] out_5,
  output [15:0] out_6,
  output [1:0] out_7
);

  wire AluSrc, Branch, clk, inverseA, inverseB, Jump, JumpSrc, MemRead, MemToReg, MemWrite, OverFlow, RegWr,
       zero;
  wire [2:0] multiplexer_1_out;
  wire [3:0] aluOp;
  wire [11:0] adder_1_out, adder_2_out, bit_extender_4_out, multiplexer_4_out, multiplexer_5_out,
       multiplexer_6_out, register_1_q;
  wire [15:0] bit_extender_1_out, bit_extender_2_out, bit_extender_3_out, multiplexer_2_out,
       multiplexer_3_out, multiplexer_7_out, ram_1_data, shifter_1_out;

  Register #(.width(12)) register_1 (.D(multiplexer_6_out), .en(1'b1), .Q(register_1_q), .clk(clk), .clr(clear));
  Clock clock_1 (.out(clk));
  Adder #(.width(12)) adder_1 (.a(12'h1), .b(register_1_q), .out(adder_1_out));  // open: cin, cout
  ROM #(.addrWidth(12), .dataWidth(16)) rom_1 (.addr(register_1_q), .data(out_2), .sel(1'b1));
  assign bit_extender_1_out = {{4{1'b0}}, out_2[11:0]};  // Bit_Extender bit_extender_1
  Branch_control branch_control_1 (.OverFlow(OverFlow), .op(out_2[15:12]), .LT(out_4[0]), .Zero(zero), .Branch(Branch));
  assign bit_extender_2_out = {{4{1'b0}}, adder_1_out};  // Bit_Extender bit_extender_2
  Shifter #(.width(16)) shifter_1 (.in(bit_extender_1_out), .\dist (4'b0100), .out(shifter_1_out));
  Multiplexer #(.select(2), .width(3), .enable("false")) multiplexer_1 (
    .in0(out_2[8:6]), .in1(out_2[5:3]), .in2(3'b111), .in3(3'b001), .out(multiplexer_1_out), .sel(out_3));
  Multiplexer #(.select(2), .width(16), .enable("false")) multiplexer_2 (
    .in0(multiplexer_7_out), .in1(bit_extender_2_out), .in2(shifter_1_out), .out(multiplexer_2_out),
    .sel(out_7));  // open: in3
  assign bit_extender_3_out = {{10{out_2[5]}}, out_2[5:0]};  // Bit_Extender bit_extender_3
  Register_File register_file_1 (
    .Write_register(multiplexer_1_out), .Write_Data(multiplexer_2_out), .Read_Data_1(out_5),
    .Read_Data_2(out_6), .RegWrite(RegWr), .read_register_1(out_2[11:9]), .read_register_2(out_2[8:6]),
    .Clk(clk), .in_7(clear));
  assign bit_extender_4_out = {{6{out_2[5]}}, out_2[5:0]};  // Bit_Extender bit_extender_4
  Multiplexer #(.width(16), .enable("false")) multiplexer_3 (
    .in0(out_6), .in1(bit_extender_3_out), .out(multiplexer_3_out), .sel(AluSrc));
  Multiplexer #(.width(12), .enable("false")) multiplexer_4 (
    .in0(out_2[11:0]), .in1(out_5[11:0]), .out(multiplexer_4_out), .sel(JumpSrc));
  Adder #(.width(12)) adder_2 (.a(adder_1_out), .b(bit_extender_4_out), .out(adder_2_out));  // open: cin, cout
  Multiplexer #(.width(12), .enable("false")) multiplexer_5 (
    .in0(adder_1_out), .in1(adder_2_out), .out(multiplexer_5_out), .sel(Branch));
  ALU alu_1 (
    .inverseA(inverseA), .inverseB(inverseB), .A(out_5), .B(multiplexer_3_out), .aluOp(aluOp),
    .Result(out_4), .zero(zero), .OverFlow(OverFlow));
  Multiplexer #(.width(12), .enable("false")) multiplexer_6 (
    .in0(multiplexer_5_out), .in1(multiplexer_4_out), .out(multiplexer_6_out), .sel(Jump));
  RAM #(.addrWidth(16), .dataWidth(16), .bus("separate")) ram_1 (
    .addr(out_4), .din(out_6), .data(ram_1_data), .str(MemWrite), .sel(1'b1), .clk(clk), .ld(MemRead),
    .clr(1'b0));
  Multiplexer #(.width(16), .enable("false")) multiplexer_7 (
    .in0(ram_1_data), .in1(out_4), .out(multiplexer_7_out), .sel(MemToReg));
  General_CtrlUnit general_ctrlunit_1 (
    .op(out_2[15:12]), .Func(out_2[2:0]), .RegWr(RegWr), .Alurc(AluSrc), .MemWrite(MemWrite),
    .MemRead(MemRead), .Jump(Jump), .Jump_Src(JumpSrc), .RegDst(out_3), .writeDataSrc(out_7),
    .MemToReg(MemToReg));
  ALU_CTRL_Unit alu_ctrl_unit_1 (
    .Op(out_2[15:12]), .func(out_2[2:0]), .aluop(aluOp), .inversA(inverseA), .inversB(inverseB));

  // Other names for the same wires on the sheet: clr = clear; Funct[2:0] = out_2[2:0]; Imm6[5:0] = out_2[5:0];
  //   Imm12[11:0] = out_2[11:0]; Rd[2:0] = out_2[5:3]; Rt[2:0] = out_2[8:6]; Rs[2:0] = out_2[11:9];
  //   Op[3:0] = out_2[15:12]; lessThan = out_4[0]; RegsDst[1:0] = out_3; writeDataSrc[1:0] = out_7

  // Notes on the sheet:
  //   contents of rom_1 (hex, n*v repeats v):
  //   a384 8354 35b 2040 2081 20c2 890a 1921 1520 14f2 4c02 1290 403b 3100 b012 55c 1b68 403f 4e9 2040
  //   2285 22c6 4e0 3100 1e06
endmodule

module Register_File (
  input  [2:0] read_register_1,
  input  [2:0] Write_register,
  input  [2:0] read_register_2,
  input  [15:0] Write_Data,
  input  RegWrite,
  input  Clk,
  input  in_7,
  output [15:0] Read_Data_1,
  output [15:0] Read_Data_2
);

  wire and_1_out, and_2_out, and_3_out, and_4_out, and_5_out, and_6_out, and_7_out, and_8_out,
       decoder_1_out0, decoder_1_out1, decoder_1_out2, decoder_1_out3, decoder_1_out4, decoder_1_out5,
       decoder_1_out6, decoder_1_out7;
  wire [15:0] R0_q, R1_q, R2_q, R3_q, R4_q, R5_q, R6_q, R7_q;

  Decoder #(.select(3), .enable("false")) decoder_1 (
    .out0(decoder_1_out0), .out1(decoder_1_out1), .out2(decoder_1_out2), .out3(decoder_1_out3),
    .out4(decoder_1_out4), .out5(decoder_1_out5), .out6(decoder_1_out6), .out7(decoder_1_out7),
    .sel(Write_register));
  and and_1 (and_1_out, decoder_1_out0, RegWrite);
  and and_2 (and_2_out, decoder_1_out1, RegWrite);
  and and_3 (and_3_out, decoder_1_out2, RegWrite);
  and and_4 (and_4_out, decoder_1_out3, RegWrite);
  and and_5 (and_5_out, decoder_1_out4, RegWrite);
  and and_6 (and_6_out, decoder_1_out5, RegWrite);
  and and_7 (and_7_out, decoder_1_out6, RegWrite);
  and and_8 (and_8_out, decoder_1_out7, RegWrite);
  Register #(.width(16)) R0 (.D({16{1'b0}}), .en(and_1_out), .Q(R0_q), .clk(Clk), .clr(in_7));
  Register #(.width(16)) R1 (.D(Write_Data), .en(and_2_out), .Q(R1_q), .clk(Clk), .clr(in_7));
  Register #(.width(16)) R2 (.D(Write_Data), .en(and_3_out), .Q(R2_q), .clk(Clk), .clr(in_7));
  Register #(.width(16)) R3 (.D(Write_Data), .en(and_4_out), .Q(R3_q), .clk(Clk), .clr(in_7));
  Register #(.width(16)) R4 (.D(Write_Data), .en(and_5_out), .Q(R4_q), .clk(Clk), .clr(in_7));
  Register #(.width(16)) R5 (.D(Write_Data), .en(and_6_out), .Q(R5_q), .clk(Clk), .clr(in_7));
  Register #(.width(16)) R6 (.D(Write_Data), .en(and_7_out), .Q(R6_q), .clk(Clk), .clr(in_7));
  Register #(.width(16)) R7 (.D(Write_Data), .en(and_8_out), .Q(R7_q), .clk(Clk), .clr(in_7));
  Multiplexer #(.select(3), .width(16), .enable("false")) multiplexer_1 (
    .in0(R0_q), .in1(R1_q), .in2(R2_q), .in3(R3_q), .in4(R4_q), .in5(R5_q), .in6(R6_q), .in7(R7_q),
    .out(Read_Data_1), .sel(read_register_1));
  Multiplexer #(.select(3), .width(16), .enable("false")) multiplexer_2 (
    .in0(R0_q), .in1(R1_q), .in2(R2_q), .in3(R3_q), .in4(R4_q), .in5(R5_q), .in6(R6_q), .in7(R7_q),
    .out(Read_Data_2), .sel(read_register_2));
endmodule

module ALU (
  input  inverseA,
  input  inverseB,
  input  [15:0] A,
  input  [15:0] B,
  input  [3:0] aluOp,
  output [15:0] Result,
  output zero,
  output OverFlow
);

  wire [0:0] and_2_out, or_2_out, or_3_out;
  wire [15:0] adder_1_out, and_1_out, multiplexer_1_out, multiplexer_2_out, not_1_out, not_2_out, or_1_out,
       shifter_1_out, shifter_2_out, shifter_3_out, shifter_4_out, xor_1_out;

  assign not_1_out = ~A;  // NOT_Gate not_1, 16 bits wide
  assign not_2_out = ~B;  // NOT_Gate not_2, 16 bits wide
  Multiplexer #(.width(16), .enable("false")) multiplexer_1 (
    .in0(A), .in1(not_1_out), .out(multiplexer_1_out), .sel(inverseA));
  Multiplexer #(.width(16), .enable("false")) multiplexer_2 (
    .in0(B), .in1(not_2_out), .out(multiplexer_2_out), .sel(inverseB));
  adder adder_1 (.A(multiplexer_1_out), .B(multiplexer_2_out), .overFlow(OverFlow), .out(adder_1_out), .C_in(inverseB));
  assign and_1_out = multiplexer_1_out & multiplexer_2_out;  // AND_Gate and_1, 16 bits wide
  assign or_1_out = multiplexer_1_out | multiplexer_2_out;  // OR_Gate or_1, 16 bits wide
  assign xor_1_out = multiplexer_1_out ^ multiplexer_2_out;  // XOR_Gate xor_1, 16 bits wide
  Shifter #(.width(16)) shifter_1 (.in(multiplexer_1_out), .\dist (multiplexer_2_out[3:0]), .out(shifter_1_out));
  Shifter #(.width(16), .shift("lr")) shifter_2 (
    .in(multiplexer_1_out), .\dist (multiplexer_2_out[3:0]), .out(shifter_2_out));
  Shifter #(.width(16), .shift("ar")) shifter_3 (
    .in(multiplexer_1_out), .\dist (multiplexer_2_out[3:0]), .out(shifter_3_out));
  Shifter #(.width(16), .shift("rl")) shifter_4 (
    .in(multiplexer_1_out), .\dist (multiplexer_2_out[3:0]), .out(shifter_4_out));
  and and_2 (and_2_out[0], OverFlow, adder_1_out[15]);
  or or_2 (or_2_out[0], zero, and_2_out[0]);
  or or_3 (or_3_out[0], zero, adder_1_out[15]);
  Multiplexer #(.select(4), .width(16), .enable("false")) multiplexer_3 (
    .in0(adder_1_out), .in1(and_1_out), .in2(or_1_out), .in3(xor_1_out), .in4(shifter_1_out),
    .in5(shifter_2_out), .in6(shifter_3_out), .in7(shifter_4_out), .in8({{15{1'b0}}, adder_1_out[15]}),
    .in9({{15{1'b0}}, and_2_out[0]}), .in10({{15{1'b0}}, or_3_out[0]}), .in11({{15{1'b0}}, or_2_out[0]}),
    .out(Result), .sel(aluOp));  // open: in12, in13, in14, in15
  nor nor_1 (zero, adder_1_out[0], adder_1_out[1], adder_1_out[2], adder_1_out[3], adder_1_out[4], adder_1_out[5], adder_1_out[6], adder_1_out[7], adder_1_out[9], adder_1_out[10], adder_1_out[11], adder_1_out[12], adder_1_out[13], adder_1_out[14], adder_1_out[15], adder_1_out[8]);
endmodule

module adder (
  input  C_in,
  input  [15:0] A,
  input  [15:0] B,
  output [15:0] out,
  output overFlow
);

  wire adder_1_cout, adder_2_cout, adder_3_cout, adder_4_cout, adder_5_cout, adder_6_cout, adder_7_cout,
       adder_8_cout, adder_9_cout, adder_10_cout, adder_11_cout, adder_12_cout, adder_13_cout, adder_14_cout,
       adder_15_cout, adder_16_cout;

  Adder #(.width(1)) adder_1 (.a(A[0]), .b(B[0]), .out(out[0]), .cin(C_in), .cout(adder_1_cout));
  Adder #(.width(1)) adder_2 (.a(A[1]), .b(B[1]), .out(out[1]), .cin(adder_1_cout), .cout(adder_2_cout));
  Adder #(.width(1)) adder_3 (.a(A[2]), .b(B[2]), .out(out[2]), .cin(adder_2_cout), .cout(adder_3_cout));
  Adder #(.width(1)) adder_4 (.a(A[3]), .b(B[3]), .out(out[3]), .cin(adder_3_cout), .cout(adder_4_cout));
  Adder #(.width(1)) adder_5 (.a(A[4]), .b(B[4]), .out(out[4]), .cin(adder_4_cout), .cout(adder_5_cout));
  Adder #(.width(1)) adder_6 (.a(A[5]), .b(B[5]), .out(out[5]), .cin(adder_5_cout), .cout(adder_6_cout));
  Adder #(.width(1)) adder_7 (.a(A[6]), .b(B[6]), .out(out[6]), .cin(adder_6_cout), .cout(adder_7_cout));
  Adder #(.width(1)) adder_8 (.a(A[7]), .b(B[7]), .out(out[7]), .cin(adder_7_cout), .cout(adder_8_cout));
  Adder #(.width(1)) adder_9 (.a(A[8]), .b(B[8]), .out(out[8]), .cin(adder_8_cout), .cout(adder_9_cout));
  Adder #(.width(1)) adder_10 (.a(A[9]), .b(B[9]), .out(out[9]), .cin(adder_9_cout), .cout(adder_10_cout));
  Adder #(.width(1)) adder_11 (.a(A[10]), .b(B[10]), .out(out[10]), .cin(adder_10_cout), .cout(adder_11_cout));
  Adder #(.width(1)) adder_12 (.a(A[11]), .b(B[11]), .out(out[11]), .cin(adder_11_cout), .cout(adder_12_cout));
  Adder #(.width(1)) adder_13 (.a(A[12]), .b(B[12]), .out(out[12]), .cin(adder_12_cout), .cout(adder_13_cout));
  Adder #(.width(1)) adder_14 (.a(A[13]), .b(B[13]), .out(out[13]), .cin(adder_13_cout), .cout(adder_14_cout));
  Adder #(.width(1)) adder_15 (.a(A[14]), .b(B[14]), .out(out[14]), .cin(adder_14_cout), .cout(adder_15_cout));
  Adder #(.width(1)) adder_16 (.a(A[15]), .b(B[15]), .out(out[15]), .cin(adder_15_cout), .cout(adder_16_cout));
  xor xor_1 (overFlow, adder_15_cout, adder_16_cout);
endmodule

module ALU_CTRL_Unit (
  input  [3:0] Op,
  input  [2:0] func,
  output [3:0] aluop,
  output inversA,
  output inversB
);

  wire and_1_out, and_2_out, and_4_out, and_5_out, and_6_out, and_7_out, and_8_out, and_9_out, and_10_out,
       and_11_out, and_13_out, and_14_out, and_15_out, and_16_out, and_17_out, not_1_out, not_2_out,
       not_3_out, not_4_out, not_5_out, not_6_out, not_7_out, not_8_out, not_9_out, not_10_out, not_11_out,
       not_12_out, not_13_out, not_14_out, not_15_out, not_16_out, not_17_out, not_18_out, not_19_out,
       not_20_out, not_21_out, not_22_out, not_23_out, not_24_out, not_25_out, not_26_out, not_27_out,
       not_28_out, not_29_out, not_30_out, not_31_out, not_32_out, not_33_out, not_34_out, not_35_out,
       not_36_out, not_37_out, not_38_out, not_39_out, not_40_out, not_41_out, not_42_out, not_43_out,
       not_44_out, not_45_out, not_46_out;

  not not_1 (not_1_out, Op[2]);
  not not_2 (not_2_out, Op[1]);
  not not_3 (not_3_out, Op[2]);
  not not_4 (not_4_out, Op[1]);
  not not_5 (not_5_out, Op[3]);
  not not_6 (not_6_out, Op[2]);
  not not_7 (not_7_out, Op[1]);
  not not_8 (not_8_out, Op[0]);
  not not_9 (not_9_out, Op[3]);
  not not_10 (not_10_out, Op[2]);
  not not_11 (not_11_out, Op[1]);
  not not_12 (not_12_out, Op[0]);
  not not_13 (not_13_out, func[2]);
  not not_14 (not_14_out, Op[3]);
  not not_15 (not_15_out, Op[2]);
  not not_16 (not_16_out, Op[1]);
  not not_17 (not_17_out, Op[2]);
  not not_18 (not_18_out, Op[1]);
  not not_19 (not_19_out, Op[3]);
  not not_20 (not_20_out, Op[3]);
  not not_21 (not_21_out, Op[2]);
  not not_22 (not_22_out, Op[1]);
  not not_23 (not_23_out, Op[0]);
  not not_24 (not_24_out, func[2]);
  not not_25 (not_25_out, func[0]);
  not not_26 (not_26_out, Op[3]);
  not not_27 (not_27_out, Op[2]);
  not not_28 (not_28_out, Op[1]);
  not not_29 (not_29_out, Op[3]);
  not not_30 (not_30_out, Op[2]);
  not not_31 (not_31_out, Op[1]);
  not not_32 (not_32_out, Op[3]);
  not not_33 (not_33_out, Op[0]);
  not not_34 (not_34_out, Op[3]);
  not not_35 (not_35_out, Op[2]);
  not not_36 (not_36_out, Op[1]);
  not not_37 (not_37_out, Op[0]);
  not not_38 (not_38_out, func[2]);
  not not_39 (not_39_out, func[0]);
  not not_40 (not_40_out, Op[3]);
  not not_41 (not_41_out, Op[1]);
  not not_42 (not_42_out, func[2]);
  not not_43 (not_43_out, func[0]);
  not not_44 (not_44_out, Op[1]);
  not not_45 (not_45_out, Op[1]);
  not not_46 (not_46_out, Op[1]);
  and and_1 (and_1_out, not_1_out, not_2_out, Op[0], func[1]);
  and and_2 (and_2_out, not_3_out, not_4_out, Op[0], func[2]);
  and and_3 (aluop[2], not_5_out, not_6_out, not_7_out, not_8_out, func[2]);
  and and_4 (and_4_out, not_9_out, not_10_out, not_11_out, not_12_out, not_13_out, func[0]);
  and and_5 (and_5_out, not_14_out, not_15_out, not_16_out, func[2], func[1]);
  and and_6 (and_6_out, not_17_out, not_18_out, Op[0], func[2]);
  and and_7 (and_7_out, not_19_out, Op[2], Op[1], Op[0]);
  and and_8 (and_8_out, not_20_out, not_21_out, not_22_out, not_23_out, not_24_out, not_25_out);
  and and_9 (and_9_out, not_26_out, not_27_out, not_28_out, func[1], func[0]);
  and and_10 (and_10_out, not_29_out, not_30_out, not_31_out, func[2], func[0]);
  and and_11 (and_11_out, not_32_out, Op[2], Op[1], not_33_out);
  and and_12 (inversA, not_34_out, not_35_out, not_36_out, not_37_out, not_38_out, func[1], not_39_out);
  and and_13 (and_13_out, not_40_out, not_41_out, not_42_out, func[1], not_43_out);
  and and_14 (and_14_out, not_44_out, Op[0], func[0]);
  and and_15 (and_15_out, not_45_out, Op[0], func[2]);
  and and_16 (and_16_out, Op[2], not_46_out);
  and and_17 (and_17_out, Op[3], Op[1]);
  or or_1 (aluop[3], and_1_out, and_2_out);
  or or_2 (aluop[1], and_4_out, and_5_out, and_6_out, and_7_out);
  or or_3 (aluop[0], and_8_out, and_9_out, and_10_out, and_11_out);
  or or_4 (inversB, and_13_out, and_14_out, and_15_out, and_16_out, and_17_out);
endmodule

module Branch_control (
  input  OverFlow,
  input  [3:0] op,
  input  LT,
  input  Zero,
  output Branch
);

  wire and_1_out, and_2_out, and_3_out, and_4_out, not_1_out, not_2_out, not_3_out, not_4_out, not_5_out,
       not_6_out, not_7_out, not_8_out, not_9_out, not_10_out, not_11_out, not_12_out, not_13_out;

  not not_1 (not_1_out, OverFlow);
  not not_2 (not_2_out, op[3]);
  not not_3 (not_3_out, op[1]);
  not not_4 (not_4_out, op[0]);
  not not_5 (not_5_out, OverFlow);
  not not_6 (not_6_out, op[3]);
  not not_7 (not_7_out, op[1]);
  not not_8 (not_8_out, Zero);
  not not_9 (not_9_out, OverFlow);
  not not_10 (not_10_out, op[1]);
  not not_11 (not_11_out, op[0]);
  not not_12 (not_12_out, OverFlow);
  not not_13 (not_13_out, LT);
  and and_1 (and_1_out, not_1_out, not_2_out, op[2], not_3_out, not_4_out, Zero);
  and and_2 (and_2_out, not_5_out, not_6_out, op[2], not_7_out, op[0], not_8_out);
  and and_3 (and_3_out, not_9_out, op[3], op[2], not_10_out, not_11_out, LT);
  and and_4 (and_4_out, not_12_out, op[3], op[2], op[1], not_13_out);
  or or_1 (Branch, and_1_out, and_2_out, and_3_out, and_4_out);
endmodule

module IF_ID (
  input  [11:0] NPC,
  input  [15:0] Instruction_Code,
  input  clk,
  input  clr,
  output [11:0] Instruction_ADD,
  output [15:0] Instruction_Code_2
);

  Register #(.width(12)) register_1 (.D(NPC), .en(1'b1), .Q(Instruction_ADD), .clk(clk), .clr(clr));
  Register #(.width(16)) register_2 (.D(Instruction_Code), .en(1'b1), .Q(Instruction_Code_2), .clk(clk), .clr(clr));
endmodule

module ID_EX (
  input  [11:0] NPC2,
  input  [15:0] A,
  input  [15:0] A_2,
  input  [15:0] B,
  input  [15:0] B_2,
  input  [15:0] Imm16,
  input  [15:0] Imm6,
  input  RegWr,
  input  AluSrc,
  input  MemWrite,
  input  MemRead,
  input  [1:0] RegDst,
  input  [1:0] WriteDataSrc,
  input  MemToReg,
  input  [3:0] aluop,
  input  inverseA,
  input  inverseB,
  input  clk,
  input  clr,
  output [11:0] NPC2_2,
  output RegWr_2,
  output AluSrc_2,
  output MemWrite_2,
  output MemRead_2,
  output [1:0] RegDst_2,
  output [1:0] WriteDataSrc_2,
  output MemToReg_2,
  output [3:0] aluop_2,
  output inverseA_2,
  output inverseB_2
);

  Register #(.width(12)) register_1 (.D(NPC2), .en(1'b1), .Q(NPC2_2), .clk(clk), .clr(clr));
  Register #(.width(16)) register_2 (.D(A), .en(1'b1), .Q(A_2), .clk(clk), .clr(clr));
  Register #(.width(16)) register_3 (.D(B), .en(1'b1), .Q(B_2), .clk(clk), .clr(clr));
  Register #(.width(16)) register_4 (.D(Imm16), .en(1'b1), .Q(Imm6), .clk(clk), .clr(clr));
  Register #(.width(15)) register_5 (
    .D({inverseB, inverseA, aluop, MemToReg, WriteDataSrc, RegDst, MemRead, MemWrite, AluSrc, RegWr}),
    .en(1'b1),
    .Q({inverseB_2, inverseA_2, aluop_2, MemToReg_2, WriteDataSrc_2, RegDst_2, MemRead_2, MemWrite_2, AluSrc_2, RegWr_2}),
    .clk(clk), .clr(clr));
endmodule

module EX_MEM (
  input  [15:0] Result,
  input  [15:0] B,
  input  RegWr,
  input  MemWrite,
  input  MemRead,
  input  [1:0] RegDst,
  input  [1:0] WriteDataSrc,
  input  MemToReg,
  input  clk,
  input  clr,
  output [15:0] Result_2,
  output [15:0] B_2,
  output RegWr_2,
  output MemWrite_2,
  output MemRead_2,
  output [1:0] RegDst_2,
  output [1:0] WriteDataSrc_2,
  output MemToReg_2
);

  Register #(.width(16)) u_Result (.D(Result), .en(1'b1), .Q(Result_2), .clk(clk), .clr(clr));
  Register #(.width(16)) u_B (.D(B), .en(1'b1), .Q(B_2), .clk(clk), .clr(clr));
  Register register_1 (
    .D({MemToReg, WriteDataSrc, RegDst, MemRead, MemWrite, RegWr}), .en(1'b1),
    .Q({MemToReg_2, WriteDataSrc_2, RegDst_2, MemRead_2, MemWrite_2, RegWr_2}), .clk(clk), .clr(clr));
endmodule

module MEM_WB (
  input  [15:0] Result,
  input  [15:0] MemData,
  input  RegWr,
  input  [1:0] RegDst,
  input  [1:0] WriteDataSrc,
  input  MemToReg,
  input  clk,
  input  clr,
  output [15:0] Result_2,
  output [15:0] MemData_2,
  output RegWr_2,
  output [1:0] RegDst_2,
  output [1:0] WriteDataSrc_2,
  output MemToReg_2
);

  Register #(.width(16)) register_1 (.D(Result), .en(1'b1), .Q(Result_2), .clk(clk), .clr(clr));
  Register #(.width(16)) register_2 (.D(MemData), .en(1'b1), .Q(MemData_2), .clk(clk), .clr(clr));
  Register #(.width(6)) register_3 (
    .D({MemToReg, WriteDataSrc, RegDst, RegWr}), .en(1'b1),
    .Q({MemToReg_2, WriteDataSrc_2, RegDst_2, RegWr_2}), .clk(clk), .clr(clr));
endmodule

module General_CtrlUnit (
  input  [3:0] op,
  input  [2:0] Func,
  output RegWr,
  output Alurc,
  output MemWrite,
  output MemRead,
  output Jump,
  output Jump_Src,
  output [1:0] RegDst,
  output [1:0] writeDataSrc,
  output MemToReg
);

  wire and_2_out, and_3_out, and_4_out, and_5_out, and_6_out, and_7_out, and_8_out, and_9_out, and_12_out,
       and_13_out, and_14_out, and_15_out, and_17_out, and_18_out, not_1_out, not_2_out, not_3_out,
       not_4_out, not_5_out, not_6_out, not_7_out, not_8_out, not_9_out, not_10_out, not_11_out, not_12_out,
       not_13_out, not_14_out, not_15_out, not_16_out, not_17_out, not_18_out, not_19_out, not_20_out,
       not_21_out, not_22_out, not_23_out, not_25_out, not_26_out, not_27_out, not_28_out, not_29_out,
       not_30_out;

  not not_1 (not_1_out, op[3]);
  not not_2 (not_2_out, op[2]);
  not not_3 (not_3_out, op[1]);
  not not_4 (not_4_out, Func[2]);
  not not_5 (not_5_out, op[3]);
  not not_6 (not_6_out, op[2]);
  not not_7 (not_7_out, op[1]);
  not not_8 (not_8_out, Func[1]);
  not not_9 (not_9_out, op[2]);
  not not_10 (not_10_out, op[0]);
  not not_11 (not_11_out, op[3]);
  not not_12 (not_12_out, op[2]);
  not not_13 (not_13_out, op[1]);
  not not_14 (not_14_out, op[3]);
  not not_15 (not_15_out, op[2]);
  not not_16 (not_16_out, op[3]);
  not not_17 (not_17_out, op[2]);
  not not_18 (not_18_out, op[3]);
  not not_19 (not_19_out, op[2]);
  not not_20 (not_20_out, op[0]);
  not not_21 (not_21_out, op[2]);
  not not_22 (not_22_out, op[1]);
  not not_23 (not_23_out, op[2]);
  not not_24 (Jump_Src, op[3]);
  and and_1 (RegDst[1], op[3], op[1]);
  not not_25 (not_25_out, op[3]);
  not not_26 (not_26_out, op[1]);
  not not_27 (not_27_out, op[0]);
  not not_28 (not_28_out, op[0]);
  not not_29 (not_29_out, op[2]);
  not not_30 (not_30_out, op[1]);
  and and_2 (and_2_out, not_1_out, not_2_out, not_3_out, not_4_out);
  and and_3 (and_3_out, not_5_out, not_6_out, not_7_out, not_8_out);
  and and_4 (and_4_out, not_9_out, not_10_out);
  and and_5 (and_5_out, not_11_out, not_12_out, not_13_out, Func[0]);
  and and_6 (and_6_out, not_14_out, op[2], op[1]);
  and and_7 (and_7_out, op[3], not_15_out, op[1]);
  and and_8 (and_8_out, not_16_out, op[1]);
  and and_9 (and_9_out, op[3], not_17_out);
  and and_10 (MemWrite, not_18_out, not_19_out, op[1], op[0]);
  and and_11 (MemRead, op[1], not_20_out);
  and and_12 (and_12_out, not_21_out, not_22_out, op[0], Func[2], Func[1]);
  and and_13 (and_13_out, op[3], not_23_out, op[0]);
  and and_14 (and_14_out, not_25_out, not_26_out);
  and and_15 (and_15_out, op[3], op[1], not_27_out);
  and and_16 (writeDataSrc[1], op[3], op[1], not_28_out);
  and and_17 (and_17_out, not_29_out, op[0], Func[2], Func[1]);
  and and_18 (and_18_out, op[3], op[0]);
  or or_1 (MemToReg, not_30_out, op[2]);
  or or_2 (RegWr, and_2_out, and_3_out, and_4_out, and_5_out, and_6_out, and_7_out);
  or or_3 (Alurc, and_8_out, and_9_out);
  or or_4 (Jump, and_12_out, and_13_out);
  or or_5 (RegDst[0], and_14_out, and_15_out);
  or or_6 (writeDataSrc[0], and_17_out, and_18_out);
endmodule
